// Logisim project lab8.circ as structural Verilog: 1 circuit, main circuit main
module main (
);

  wire button_1_out, CLK, clock_1_out, sub, subtractor_1_bout;
  wire [0:0] shifter_2_out;
  wire [14:0] shifter_2_out_2;
  wire [15:0] Div, Dividend_Remainder_q, Quotient_q, shifter_1_out, subtractor_1_out;

  Clock clock_1 (.out(clock_1_out));
  or or_1 (CLK, clock_1_out, button_1_out);
  Button button_1 (.out(button_1_out));
  Shifter #(.width(16), .shift("lr")) shifter_1 (.in(Div), .\dist (4'b0001), .out(shifter_1_out));
  Register #(.width(16)) Divisor (.D(shifter_1_out), .Q(Div), .clk(CLK));  // open: en, clr
  Subtractor #(.width(16)) subtractor_1 (
    .a(Dividend_Remainder_q), .b(Div), .out(subtractor_1_out), .bout(subtractor_1_bout));  // open: bin
  not not_1 (sub, subtractor_1_bout);
  Shifter #(.width(16)) shifter_2 (.in(Quotient_q), .\dist (4'b0001), .out({shifter_2_out_2, shifter_2_out[0]}));
  // Probe on Div
  // Probe on Dividend_Remainder_q
  Register #(.width(16)) Dividend_Remainder (
    .D(subtractor_1_out), .en(sub), .Q(Dividend_Remainder_q), .clk(CLK));  // open: clr
  // Probe on Quotient_q
  Register #(.width(16)) Quotient (.D({shifter_2_out_2, sub}), .Q(Quotient_q), .clk(CLK));  // open: en, clr
endmodule
