// Logisim project siz24_lab8.circ as structural Verilog: 2 circuits, main circuit main
module main (
);

  wire Add, button_1_out, CLK, clock_1_out, Done;
  wire [7:0] Multiplier_q, shifter_2_out;
  wire [15:0] adder_1_out, Multiplicand_q, Product_q, shifter_1_out;

  Clock clock_1 (.out(clock_1_out));
  or or_1 (CLK, clock_1_out, button_1_out);
  Button button_1 (.out(button_1_out));
  LED u_Done (.in(Done));
  Shifter #(.width(16)) shifter_1 (.in(Multiplicand_q), .\dist (4'b0001), .out(shifter_1_out));
  Register #(.width(16)) Multiplicand (.D(shifter_1_out), .Q(Multiplicand_q), .clk(CLK));  // open: en, clr
  Shifter #(.shift("lr")) shifter_2 (.in(Multiplier_q), .\dist (3'b001), .out(shifter_2_out));
  Adder #(.width(16)) adder_1 (.a(Product_q), .b(Multiplicand_q), .out(adder_1_out));  // open: cin, cout
  // Probe on Multiplier_q
  Register Multiplier (.D(shifter_2_out), .Q(Multiplier_q), .clk(CLK));  // open: en, clr
  Register #(.width(16)) Product (.D(adder_1_out), .en(Add), .Q(Product_q), .clk(CLK));  // open: clr
  // Probe on adder_1_out
  Comparator comparator_1 (.a({8{1'b0}}), .b(Multiplier_q), .eq(Done));  // open: gt, lt
  Comparator #(.width(1)) comparator_2 (.a(Multiplier_q[0]), .b(1'b1), .eq(Add));  // open: gt, lt
  // Probe on Product_q
endmodule

module Division (
);

  wire button_1_out, CLK, clock_1_out, sub, subtractor_1_bout;
  wire [15:0] Dividend_Remainder_q, Divisor_q, Quotient_q, shifter_1_out, shifter_2_out, subtractor_1_out;

  Clock clock_1 (.out(clock_1_out));
  or or_1 (CLK, clock_1_out, button_1_out);
  Button button_1 (.out(button_1_out));
  Shifter #(.width(16), .shift("lr")) shifter_1 (.in(Divisor_q), .\dist (4'b0001), .out(shifter_1_out));
  Register #(.width(16)) Divisor (.D(shifter_1_out), .Q(Divisor_q), .clk(CLK));  // open: en, clr
  Shifter #(.width(16)) shifter_2 (.in(Quotient_q), .\dist (4'b0001), .out(shifter_2_out));
  Subtractor #(.width(16)) subtractor_1 (
    .a(Dividend_Remainder_q), .b(Divisor_q), .out(subtractor_1_out), .bout(subtractor_1_bout));  // open: bin
  not not_1 (sub, subtractor_1_bout);
  // Probe on Divisor_q
  Register #(.width(16)) Quotient (.D({shifter_2_out[15:1], sub}), .Q(Quotient_q), .clk(CLK));  // open: en, clr
  Register #(.width(16)) Dividend_Remainder (
    .D(subtractor_1_out), .en(sub), .Q(Dividend_Remainder_q), .clk(CLK));  // open: clr
  // Probe on Quotient_q
  // Probe on Dividend_Remainder_q
endmodule
