// Logisim project siz24_lab9.circ as structural Verilog: 2 circuits, main circuit main
module main (
  input  is_call,
  input  is_ret,
  input  [15:0] PC,
  output [15:0] return_address
);

  wire CLK;

  Clock clock_1 (.out(CLK));
  // Probe on return_address
  // Probe on PC
  Return_Stack return_stack_1 (.CLK(CLK), .is_call(is_call), .is_ret(is_ret), .PC(PC), .return_address(return_address));

  // Other names for the same wires on the sheet: ret_addr[15:0] = return_address

  // Notes on the sheet:
  //   hex
  //   hex
  //   Return Stack
endmodule

module Return_Stack (
  input  CLK,
  input  is_call,
  input  is_ret,
  input  [15:0] PC,
  output [15:0] return_address
);

  wire adder_1_cout, spWE;
  wire [7:0] multiplexer_1_out, multiplexer_2_out, sp, sp_1, sp_1_t;
  wire [15:0] PC_1;

  // Probe on return_address
  or or_1 (spWE, is_call, is_ret);
  Adder adder_1 (.a(sp), .b(8'h1), .out(sp_1), .cout(adder_1_cout));  // open: cin
  Subtractor subtractor_1 (.a(sp), .b(8'h1), .out(sp_1_t), .bin(adder_1_cout));  // open: bout
  // Probe on PC
  // Probe on PC_1
  Adder #(.width(16)) adder_2 (.a(PC), .b(16'h1), .out(PC_1));  // open: cin, cout
  Multiplexer #(.width(8)) multiplexer_1 (.in0(sp), .in1(sp_1_t), .out(multiplexer_1_out), .sel(is_ret));  // open: en
  Register u_sp (.D(multiplexer_2_out), .en(spWE), .Q(sp), .clk(CLK));  // open: clr
  Multiplexer #(.width(8)) multiplexer_2 (
    .in0(sp_1_t), .in1(sp_1), .out(multiplexer_2_out), .sel(is_call));  // open: en
  RAM #(.dataWidth(16), .bus("separate")) ram_1 (
    .addr(multiplexer_1_out), .din(PC_1), .data(return_address), .str(is_call), .clk(CLK));  // open: sel, ld, clr

  // Other names for the same wires on the sheet: ret_addr[15:0] = return_address

  // Notes on the sheet:
  //   hex
  //   hex
  //   hex
endmodule
