// Logisim project siz24.circ as structural Verilog: 7 circuits, main circuit main
// ROM
module main (
);

  wire aluSrc, CLK, display, HALT, I_Type, is_call, is_ret, KbRead, MemWrite, RegWrite, should_jump, TTY;
  wire [1:0] RegDataSrc;
  wire [2:0] aluOp, ConditionalBranches, PCSrc, rd, rs, rt;
  wire [3:0] Display_digits1, Display_digits2, Display_digits3, Display_digits4;
  wire [6:0] bit_extender_2_out, kb;
  wire [15:0] aluOut, bit_extender_1_out, Data, imm, multiplexer_1_out, multiplexer_2_out, PC, ret, rsOut,
       rtOut;
  wire [19:0] rom_1_data;

  Clock clock_1 (.out(CLK));
  assign bit_extender_1_out = {{9{1'b0}}, kb};  // Bit_Extender bit_extender_1
  LED u_HALT (.in(HALT));
  Hex_Digit_Display hex_digit_display_1 (.value(Display_digits4));  // open: dp
  Display u_Display (
    .data(rsOut), .WE(display), .CLK(CLK), .Digits4(Display_digits4), .Digits3(Display_digits3),
    .Digits2(Display_digits2), .Digits1(Display_digits1));
  PC_Control pc_control_1 (
    .HALT(HALT), .sxt_imm8(imm), .imm16(imm), .ret(ret), .Output(PC), .CLK(CLK), .PCSrc(PCSrc),
    .rsOut(rsOut), .should_jump(should_jump));
  Hex_Digit_Display hex_digit_display_2 (.value(Display_digits3));  // open: dp
  Hex_Digit_Display hex_digit_display_3 (.value(Display_digits2));  // open: dp
  Register_File Register_File (
    .rd(rd), .rs(rs), .rt(rt), .I_Type(I_Type), .Data(multiplexer_1_out), .rs_out(rsOut), .rt_out(rtOut),
    .CLK(CLK), .WE(RegWrite));
  Multiplexer #(.select(2), .width(16)) multiplexer_1 (
    .in0(Data), .in1(imm), .in2(aluOut), .in3(bit_extender_1_out), .out(multiplexer_1_out), .sel(RegDataSrc));  // open: en
  Hex_Digit_Display hex_digit_display_4 (.value(Display_digits1));  // open: dp
  ROM #(.addrWidth(16), .dataWidth(20)) rom_1 (.addr(PC), .data(rom_1_data));  // open: sel
  Keyboard keyboard_1 (.clk(CLK), .re(KbRead), .data(kb));  // open: clr, avail
  Multiplexer #(.width(16)) multiplexer_2 (.in0(rtOut), .in1(imm), .out(multiplexer_2_out), .sel(aluSrc));  // open: en
  Control Control (
    .Instruction(rom_1_data), .HALT(HALT), .is_call(is_call), .Display(display), .is_ret(is_ret),
    .aluOp(aluOp), .MemWrite(MemWrite), .I_Type(I_Type), .RegWrite(RegWrite), .PCSrc(PCSrc),
    .RegDataSrc(RegDataSrc), .rs(rs), .rt(rt), .rd(rd), .ConditionalBranch(ConditionalBranches),
    .aluSrc(aluSrc), .imm(imm), .KbRead(KbRead), .out(TTY));
  ALU alu_1 (
    .A(rsOut), .B(multiplexer_2_out), .aluOut(aluOut), .aluOp(aluOp),
    .ConditionalBranch(ConditionalBranches), .ConditionSatisfies(should_jump));
  Bit_Extender #(.in_width(16), .out_width(7)) bit_extender_2 (.in(rsOut), .out(bit_extender_2_out));
  TTY tty_1 (.data(bit_extender_2_out), .clk(CLK), .we(TTY));  // open: clr
  Return_Stack Return_Stack (.CLK(CLK), .is_call(is_call), .is_ret(is_ret), .PC(PC), .return_address(ret));
  RAM #(.addrWidth(16), .dataWidth(16), .bus("separate")) ram_1 (
    .addr(aluOut), .din(rtOut), .data(Data), .str(MemWrite), .clk(CLK));  // open: sel, ld, clr

  // Notes on the sheet:
  //   00 ld
  //   01 li / lui
  //   10 aluOp
  //   11 in
  //   ROM
  //   Keyboard
  //   RAM
  //   TTY
endmodule

module Display (
  input  [15:0] data,
  input  WE,
  input  CLK,
  output [3:0] Digits4,
  output [3:0] Digits3,
  output [3:0] Digits2,
  output [3:0] Digits1
);

  Register #(.width(16)) register_1 (
    .D(data), .en(WE), .Q({Digits4, Digits3, Digits2, Digits1}), .clk(CLK));  // open: clr
endmodule

module ALU (
  input  [15:0] A,
  input  [2:0] ConditionalBranch,
  input  [15:0] B,
  input  [2:0] aluOp,
  output ConditionSatisfies,
  output [15:0] aluOut
);

  wire neg, not_2_out, not_3_out, not_4_out, rs__0, zero;
  wire [15:0] add, \and , \not , \or , sleft, sright, sub;

  // Probe on A
  // Probe on B
  Adder #(.width(16)) adder_1 (.a(A), .b(B), .out(add));  // open: cin, cout
  Subtractor #(.width(16)) subtractor_1 (.a(A), .b(B), .out(sub));  // open: bin, bout
  Comparator #(.width(16)) comparator_1 (.a(sub), .b({16{1'b0}}), .eq(zero), .lt(neg));  // open: gt
  assign \and  = A & B;  // AND_Gate and_1, 16 bits wide
  assign \or  = A | B;  // OR_Gate or_1, 16 bits wide
  assign \not  = ~B;  // NOT_Gate not_1, 16 bits wide
  Shifter #(.width(16)) shifter_1 (.in(A), .\dist (B[3:0]), .out(sleft));
  Shifter #(.width(16), .shift("lr")) shifter_2 (.in(A), .\dist (B[3:0]), .out(sright));
  // Probe on aluOut
  Multiplexer #(.select(3), .width(16)) multiplexer_1 (
    .in0(\not ), .in1(\and ), .in2(\or ), .in3(add), .in4(sub), .in5(sleft), .in6(sright), .out(aluOut),
    .sel(aluOp));  // open: in7, en
  // NOT_Gate not_2 has open pins: in=open, out=not_2_out
  // NOT_Gate not_3 has open pins: in=open, out=not_3_out
  // NOT_Gate not_4 has open pins: in=open, out=not_4_out
  Multiplexer #(.select(3)) multiplexer_2 (
    .in0(neg), .in1(not_2_out), .in2(zero), .in3(not_3_out), .in4(rs__0), .in5(not_4_out),
    .out(ConditionSatisfies), .sel(ConditionalBranch));  // open: in6, in7, en
  Comparator #(.width(16)) comparator_2 (.a(A), .b({16{1'b0}}), .eq(rs__0));  // open: gt, lt

  // Other names for the same wires on the sheet: CB[2:0] = ConditionalBranch; should_jmp = ConditionSatisfies

  // Notes on the sheet:
  //   comparing rs and rt for conditional branches
  //   000 not
  //   001 and
  //   010 or
  //   011 add
  //   100 sub
  //   101 logical left shifting
  //   110 logical right shifting
  //   comparing rs and 0 for conditional branches
  //   000 blt
  //   001 bge
  //   010 beq
  //   011 bne
  //   100 bez
  //   101 bnz
endmodule

module Register_File (
  input  [2:0] rd,
  input  [2:0] rs,
  input  [2:0] rt,
  input  I_Type,
  input  [15:0] Data,
  input  CLK,
  input  WE,
  output [15:0] rs_out,
  output [15:0] rt_out
);

  wire demultiplexer_1_out0, demultiplexer_1_out1, demultiplexer_1_out2, demultiplexer_1_out3,
       demultiplexer_1_out4, demultiplexer_1_out5, demultiplexer_1_out6, demultiplexer_1_out7;
  wire [2:0] multiplexer_1_out;
  wire [15:0] r1, r2, r3, r4, r5, r6, r7;

  Demultiplexer #(.select(3)) demultiplexer_1 (
    .out0(demultiplexer_1_out0), .out1(demultiplexer_1_out1), .out2(demultiplexer_1_out2),
    .out3(demultiplexer_1_out3), .out4(demultiplexer_1_out4), .out5(demultiplexer_1_out5),
    .out6(demultiplexer_1_out6), .out7(demultiplexer_1_out7), .in(WE), .sel(multiplexer_1_out));  // open: en
  Multiplexer #(.width(3)) multiplexer_1 (.in0(rd), .in1(rt), .out(multiplexer_1_out), .sel(I_Type));  // open: en
  Register #(.width(16)) u_r1 (.D(Data), .en(demultiplexer_1_out1), .Q(r1), .clk(CLK));  // open: clr
  Register #(.width(16)) u_r2 (.D(Data), .en(demultiplexer_1_out2), .Q(r2), .clk(CLK));  // open: clr
  Register #(.width(16)) u_r3 (.D(Data), .en(demultiplexer_1_out3), .Q(r3), .clk(CLK));  // open: clr
  Register #(.width(16)) u_r4 (.D(Data), .en(demultiplexer_1_out4), .Q(r4), .clk(CLK));  // open: clr
  Register #(.width(16)) u_r5 (.D(Data), .en(demultiplexer_1_out5), .Q(r5), .clk(CLK));  // open: clr
  Register #(.width(16)) u_r6 (.D(Data), .en(demultiplexer_1_out6), .Q(r6), .clk(CLK));  // open: clr
  Register #(.width(16)) u_r7 (.D(Data), .en(demultiplexer_1_out7), .Q(r7), .clk(CLK));  // open: clr
  Multiplexer #(.select(3), .width(16)) multiplexer_2 (
    .in0({16{1'b0}}), .in1(r1), .in2(r2), .in3(r3), .in4(r4), .in5(r5), .in6(r6), .in7(r7), .out(rs_out),
    .sel(rs));  // open: en
  Multiplexer #(.select(3), .width(16)) multiplexer_3 (
    .in0({16{1'b0}}), .in1(r1), .in2(r2), .in3(r3), .in4(r4), .in5(r5), .in6(r6), .in7(r7), .out(rt_out),
    .sel(rt));  // open: en

  // Other names for the same wires on the sheet: RegWrite = WE

  // Notes on the sheet:
  //   r0(constant 0)
endmodule

module Return_Stack (
  input  CLK,
  input  is_call,
  input  is_ret,
  input  [15:0] PC,
  output [15:0] return_address
);

  wire adder_1_cout, spWE;
  wire [7:0] multiplexer_1_out, multiplexer_2_out, sp, sp_1, sp_1_t;
  wire [15:0] PC_1;

  // Probe on return_address
  or or_1 (spWE, is_call, is_ret);
  Adder adder_1 (.a(sp), .b(8'h1), .out(sp_1), .cout(adder_1_cout));  // open: cin
  Subtractor subtractor_1 (.a(sp), .b(8'h1), .out(sp_1_t), .bin(adder_1_cout));  // open: bout
  // Probe on PC
  // Probe on PC_1
  Adder #(.width(16)) adder_2 (.a(PC), .b(16'h1), .out(PC_1));  // open: cin, cout
  Multiplexer #(.width(8)) multiplexer_1 (.in0(sp), .in1(sp_1_t), .out(multiplexer_1_out), .sel(is_ret));  // open: en
  Multiplexer #(.width(8)) multiplexer_2 (
    .in0(sp_1_t), .in1(sp_1), .out(multiplexer_2_out), .sel(is_call));  // open: en
  Register u_sp (.D(multiplexer_2_out), .en(spWE), .Q(sp), .clk(CLK));  // open: clr
  RAM #(.dataWidth(16), .bus("separate")) ram_1 (
    .addr(multiplexer_1_out), .din(PC_1), .data(return_address), .str(is_call), .clk(CLK));  // open: sel, ld, clr

  // Other names for the same wires on the sheet: ret_addr[15:0] = return_address
endmodule

module PC_Control (
  input  CLK,
  input  HALT,
  input  should_jump,
  input  [2:0] PCSrc,
  input  [15:0] sxt_imm8,
  input  [15:0] rsOut,
  input  [15:0] imm16,
  input  [15:0] ret,
  output [15:0] Output
);

  wire not_1_out;
  wire [15:0] adder_1_out, adder_2_out, multiplexer_1_out, multiplexer_2_out;

  Adder #(.width(16)) adder_1 (.a(Output), .b(16'h1), .out(adder_1_out));  // open: cin, cout
  Adder #(.width(16)) adder_2 (.a(Output), .b(sxt_imm8), .out(adder_2_out));  // open: cin, cout
  Multiplexer #(.width(16)) multiplexer_1 (
    .in0(adder_1_out), .in1(adder_2_out), .out(multiplexer_1_out), .sel(should_jump));  // open: en
  Multiplexer #(.select(3), .width(16)) multiplexer_2 (
    .in0(adder_1_out), .in1(multiplexer_1_out), .in2(rsOut), .in3(imm16), .in4(ret), .out(multiplexer_2_out),
    .sel(PCSrc));  // open: in5, in6, in7, en
  not not_1 (not_1_out, HALT);
  Register #(.width(16)) PC (.D(multiplexer_2_out), .en(not_1_out), .Q(Output), .clk(CLK));  // open: clr

  // Notes on the sheet:
  //   000 PC+1
  //   010 jr
  //   011 j / call
  //   100 ret
  //   001 conditional braches
endmodule

module Control (
  input  [19:0] Instruction,
  output HALT,
  output is_call,
  output [15:0] imm,
  output Display,
  output is_ret,
  output [2:0] aluOp,
  output MemWrite,
  output I_Type,
  output KbRead,
  output out,
  output [2:0] ConditionalBranch,
  output [2:0] rs,
  output [2:0] PCSrc,
  output [2:0] rt,
  output aluSrc,
  output [2:0] rd,
  output [1:0] RegDataSrc,
  output RegWrite
);

  wire add, adi, alu, \and , ani, beq, bez, bge, blt, bne, bnz, CB, j, jr, ld, li, lui, \not , not_1_out,
       \or , or_1_out, or_2_out, or_3_out, or_4_out, or_5_out, or_6_out, or_7_out, or_8_out, or_10_out,
       or_12_out, or_14_out, or_15_out, ori, sbi, shl, shr, sli, sri, sub;
  wire [1:0] immSrc;
  wire [15:0] bit_extender_2_out, bit_extender_3_out, imm8Out, zxt_imm5;

  assign zxt_imm5 = {{11{1'b0}}, Instruction[4:0]};  // Bit_Extender bit_extender_1
  assign bit_extender_2_out = {{8{Instruction[7]}}, Instruction[7:0]};  // Bit_Extender bit_extender_2
  or or_1 (or_1_out, li, ani, ori);
  assign bit_extender_3_out = {{8{1'b0}}, Instruction[7:0]};  // Bit_Extender bit_extender_3
  Multiplexer #(.width(16)) multiplexer_1 (
    .in0(bit_extender_2_out), .in1(bit_extender_3_out), .out(imm8Out), .sel(or_1_out));  // open: en
  Demultiplexer #(.select(5)) demultiplexer_1 (
    .out0(HALT), .out1(Display), .out2(li), .out3(lui), .out4(ld), .out5(MemWrite), .out6(add), .out7(sub),
    .out8(\and ), .out9(\or ), .out10(\not ), .out11(shl), .out12(shr), .out13(adi), .out14(sbi),
    .out15(ani), .out16(ori), .out17(sli), .out18(sri), .out19(blt), .out20(bge), .out21(beq), .out22(bne),
    .out23(bez), .out24(bnz), .out25(jr), .out26(is_ret), .out27(KbRead), .out28(out), .in(not_1_out),
    .sel(Instruction[18:14]));  // open: out29, out30, out31, en
  not not_1 (not_1_out, Instruction[19]);
  Demultiplexer #(.select(3)) demultiplexer_2 (
    .out0(j), .out1(is_call), .in(Instruction[19]), .sel(Instruction[18:16]));  // open: out2, out3, out4, out5, out6, out7, en
  or or_2 (or_2_out, shr, sri);
  or or_3 (or_3_out, j, is_call);
  or or_4 (or_4_out, li, lui);
  or or_5 (or_5_out, \or , ori, or_6_out);
  or or_6 (or_6_out, add, adi, ld, MemWrite);
  or or_7 (or_7_out, sub, sbi);
  or or_8 (or_8_out, shl, sli);
  Priority_Encoder priority_encoder_1 (
    .in0(1'b1), .in1(CB), .in2(jr), .in3(or_3_out), .in4(is_ret), .out(PCSrc));  // open: in5, in6, in7, en_in, gs, en_out
  Priority_Encoder #(.select(2)) priority_encoder_2 (
    .in0(1'b1), .in1(or_4_out), .in2(alu), .in3(KbRead), .out(RegDataSrc));  // open: gs, en_out, en_in
  or or_9 (RegWrite, li, lui, ld, add, sub, \and , \or , \not , KbRead, shl, shr, adi, sbi, ani, ori, sli, sri);
  or or_10 (or_10_out, \and , ani);
  Priority_Encoder priority_encoder_3 (
    .in0(1'b1), .in1(or_10_out), .in2(or_5_out), .in3(or_6_out), .in4(or_7_out), .in5(or_8_out),
    .in6(or_2_out), .out(aluOp));  // open: in7, en_in, gs, en_out
  or or_11 (alu, add, sub, \and , \or , \not , shl, shr, adi, sbi, ani, ori, sli, sri);
  or or_12 (or_12_out, ld, MemWrite);
  or or_13 (I_Type, li, lui, adi, sbi, ani, ori, sli, sri);
  Multiplexer #(.select(2), .width(16)) multiplexer_2 (
    .in0(imm8Out), .in1(Instruction[15:0]), .in2(zxt_imm5), .in3({Instruction[7:0], {8{1'b0}}}), .out(imm),
    .sel(immSrc));  // open: en
  Priority_Encoder priority_encoder_4 (
    .in0(1'b1), .in1(bge), .in2(beq), .in3(bne), .in4(bez), .in5(bnz), .out(ConditionalBranch));  // open: in6, in7, en_in, gs, en_out
  Priority_Encoder #(.select(1)) priority_encoder_5 (
    .in0(1'b1), .in1(or_14_out), .out(aluSrc));  // open: gs, en_out, en_in
  or or_14 (or_14_out, I_Type, ld, MemWrite);
  buf or_15 (or_15_out, or_12_out);  // OR_Gate
  Priority_Encoder #(.select(2)) priority_encoder_6 (
    .in0(1'b1), .in1(or_15_out), .in2(or_12_out), .in3(lui), .out(immSrc));  // open: gs, en_out, en_in
  // Probe on immSrc
  or or_16 (CB, blt, bge, beq, bne, bez, bnz);

  assign rd = Instruction[7:5];
  assign rs = Instruction[13:11];
  assign rt = Instruction[10:8];

  // Other names for the same wires on the sheet: call = is_call; _0 = Instruction[0]; imm5[4:0] = Instruction[4:0];
  //   imm8[7:0] = Instruction[7:0]; imm8__8[15:8] = Instruction[7:0]; imm16[15:0] = Instruction[15:0];
  //   _1 = Instruction[1]; _2 = Instruction[2]; _3 = Instruction[3]; _4 = Instruction[4]; _5 = Instruction[5];
  //   _6 = Instruction[6]; _7 = Instruction[7]; _8 = Instruction[8]; _9 = Instruction[9]; _10 = Instruction[10];
  //   _11 = Instruction[11]; _12 = Instruction[12]; _13 = Instruction[13]; _14 = Instruction[14];
  //   R_I_Opcode[4:0] = Instruction[18:14]; _15 = Instruction[15]; in = KbRead; _16 = Instruction[16];
  //   J_Opcode[2:0] = Instruction[18:16]; _17 = Instruction[17]; _18 = Instruction[18]; _19 = Instruction[19];
  //   J_Type = Instruction[19]; put = Display; ret = is_ret; st = MemWrite

  // Notes on the sheet:
  //   Basic Instructions
  //   PC+1
  //   data
  //   not
  //   blt
  //   I-Type that would affect
  //   the destination register
  //   rt
  //   imm8Out
  //   Conditional Branches
endmodule
